// Logisim project display_control.circ as structural Verilog: 1 circuit, main circuit main
module main (
  input  [7:0] in_1,
  input  in_2
);

  wire A, B, C, D, E, F, G, H;

  Pull_Resistor #(.pull(1)) pull_resistor_1 (.node({H, G, F, E, D, C, B, A}));
  assign {H, G, F, E, D, C, B, A} = in_2 ? ~in_1 : 8'bz;  // Controlled_Inverter controlled_inverter_1
  _7_Segment_Display #(.active("false")) u_7_segment_display_1 (
    .g(G), .f(F), .a(A), .b(B), .e(E), .d(D), .c(C), .dp(H));
endmodule
