// Logisim project L01_example_AND_ver01.circ as structural Verilog: 1 circuit, main circuit main
module main (
  input  q,
  input  p,
  output y
);

  wire transistor_1_out;

  Transistor #(.\type ("n")) transistor_1 (.in(1'b1), .out(transistor_1_out), .gate(q));
  Transistor #(.\type ("n")) transistor_2 (.in(transistor_1_out), .out(y), .gate(p));
  Pull_Resistor pull_resistor_1 (.node(y));

  // Notes on the sheet:
  //   AND gate: NMOS + pull-down resistor
endmodule
