// Logisim project L01_example_BUF_ver01.circ as structural Verilog: 1 circuit, main circuit main
// q
module main (
  input  p,
  output y
);

  Transistor #(.\type ("n")) transistor_1 (.in(1'b1), .out(y), .gate(p));
  Transistor transistor_2 (.in(1'b0), .out(y), .gate(p));

  // Notes on the sheet:
  //   Buffer: NMOS + PMOS
endmodule
