// Logisim project L01_example_XOR_ver02.circ as structural Verilog: 1 circuit, main circuit main
module main (
  input  p,
  input  q,
  output y
);

  wire pull_resistor_1_node, transistor_5_out;

  Transistor transistor_1 (.in(p), .out(y), .gate(q));
  Transistor #(.\type ("n")) transistor_2 (.in(transistor_5_out), .out(y), .gate(q));
  Transistor transistor_3 (.in(q), .out(y), .gate(p));
  Transistor #(.\type ("n")) transistor_4 (.in(q), .out(y), .gate(transistor_5_out));
  Pull_Resistor #(.pull(1)) pull_resistor_1 (.node(pull_resistor_1_node));
  Transistor transistor_5 (.in(pull_resistor_1_node), .out(transistor_5_out), .gate(p));
  Transistor #(.\type ("n")) transistor_6 (.in(1'b0), .out(transistor_5_out), .gate(p));

  // Notes on the sheet:
  //   XOR: 2 NOT + transmission gate
endmodule
