// Logisim project L03_example_LED_line_NOR.circ as structural Verilog: 1 circuit, main circuit main
module main (
  input  a,
  input  b,
  input  c,
  input  d,
  input  e,
  output x
);

  wire nor_1_out, nor_2_out, nor_3_out, nor_4_out, nor_5_out, nor_6_out, nor_7_out, nor_8_out, nor_9_out,
       nor_10_out, nor_11_out, nor_12_out;

  nor nor_1 (nor_1_out, 1'b0, d);
  nor nor_2 (nor_2_out, 1'b0, c);
  nor nor_3 (nor_3_out, 1'b0, b);
  nor nor_4 (nor_4_out, 1'b0, b);
  nor nor_5 (nor_5_out, 1'b0, a);
  nor nor_6 (nor_6_out, 1'b0, a);
  nor nor_7 (nor_7_out, nor_1_out, e);
  nor nor_8 (nor_8_out, nor_2_out, d);
  nor nor_9 (nor_9_out, nor_3_out, c);
  nor nor_10 (nor_10_out, nor_4_out, e);
  nor nor_11 (nor_11_out, nor_5_out, b);
  nor nor_12 (nor_12_out, nor_6_out, d);
  nor nor_13 (x, nor_7_out, nor_8_out, nor_9_out, nor_10_out, nor_11_out, nor_12_out);
endmodule
