// Logisim project L03_example_div3_NAND.circ as structural Verilog: 1 circuit, main circuit main
module main (
  input  a,
  input  b,
  input  c,
  input  d,
  input  e,
  output x
);

  wire nand_1_out, nand_2_out, nand_3_out, nand_4_out, nand_5_out, nand_6_out, nand_7_out, nand_8_out,
       nand_9_out, nand_10_out, nand_11_out, nand_12_out, nand_13_out, nand_14_out, nand_15_out, nand_16_out;

  nand nand_1 (nand_1_out, 1'b1, a);
  nand nand_2 (nand_2_out, 1'b1, b);
  nand nand_3 (nand_3_out, 1'b1, c);
  nand nand_4 (nand_4_out, 1'b1, d);
  nand nand_5 (nand_5_out, 1'b1, e);
  nand nand_6 (nand_6_out, nand_1_out, nand_2_out, nand_3_out, nand_4_out, nand_5_out);
  nand nand_7 (nand_7_out, nand_1_out, nand_2_out, nand_3_out, d, e);
  nand nand_8 (nand_8_out, nand_1_out, nand_2_out, c, d, nand_5_out);
  nand nand_9 (nand_9_out, nand_1_out, b, nand_3_out, nand_4_out, e);
  nand nand_10 (nand_10_out, nand_1_out, b, c, nand_4_out, nand_5_out);
  nand nand_11 (nand_11_out, nand_1_out, b, c, d, e);
  nand nand_12 (nand_12_out, a, nand_2_out, nand_3_out, d, nand_5_out);
  nand nand_13 (nand_13_out, a, nand_2_out, c, nand_4_out, e);
  nand nand_14 (nand_14_out, a, b, nand_3_out, nand_4_out, nand_5_out);
  nand nand_15 (nand_15_out, a, b, nand_3_out, d, e);
  nand nand_16 (nand_16_out, a, b, c, d, nand_5_out);
  nand nand_17 (x, nand_6_out, nand_7_out, nand_8_out, nand_9_out, nand_10_out, nand_11_out, nand_12_out, nand_13_out, nand_14_out, nand_15_out, nand_16_out);
endmodule
