// Logisim project L03_example_div3_NOR.circ as structural Verilog: 1 circuit, main circuit main
module main (
  input  a,
  input  b,
  input  c,
  input  d,
  input  e,
  output x
);

  wire not_1_out, not_2_out, not_3_out, not_4_out, not_5_out, or_1_out, or_2_out, or_3_out, or_4_out,
       or_5_out, or_6_out, or_7_out, or_8_out, or_9_out, or_10_out, or_11_out, or_12_out, or_13_out,
       or_14_out, or_15_out;

  not not_1 (not_1_out, a);
  not not_2 (not_2_out, b);
  not not_3 (not_3_out, c);
  not not_4 (not_4_out, d);
  not not_5 (not_5_out, e);
  or or_1 (or_1_out, a, b, d, not_5_out);
  or or_2 (or_2_out, a, c, not_4_out, e);
  or or_3 (or_3_out, a, b, not_3_out, d);
  or or_4 (or_4_out, a, b, not_3_out, not_5_out);
  or or_5 (or_5_out, a, not_3_out, d, not_5_out);
  or or_6 (or_6_out, a, not_2_out, c, e);
  or or_7 (or_7_out, a, not_2_out, c, not_4_out);
  or or_8 (or_8_out, a, not_2_out, not_4_out, e);
  or or_9 (or_9_out, not_2_out, c, not_4_out, e);
  or or_10 (or_10_out, not_1_out, b, c, d);
  or or_11 (or_11_out, not_1_out, c, d, not_5_out);
  or or_12 (or_12_out, not_1_out, b, not_4_out, not_5_out);
  or or_13 (or_13_out, not_1_out, b, not_3_out, e);
  or or_14 (or_14_out, not_1_out, not_2_out, not_3_out, d);
  or or_15 (or_15_out, not_1_out, not_2_out, not_3_out, not_5_out);
  and and_1 (x, or_1_out, or_2_out, or_3_out, or_4_out, or_5_out, or_6_out, or_7_out, or_8_out, or_9_out, or_10_out, or_11_out, or_12_out, or_13_out, or_14_out, or_15_out);
endmodule
