// Logisim project L05_example_Func01.circ as structural Verilog: 5 circuits, main circuit main
module main (
  input  a,
  input  b,
  input  c,
  input  d,
  input  e,
  output x_gates,
  output x_mux,
  output x_demux,
  output x_rom
);

  FUNC01_Gates func01_gates_1 (.a(a), .b(b), .c(c), .d(d), .e(e), .x(x_gates));
  FUNC01_Mux func01_mux_1 (.a(a), .b(b), .c(c), .d(d), .e(e), .x(x_mux));
  FUNC01_Demux func01_demux_1 (.a(a), .b(b), .c(c), .d(d), .e(e), .x(x_demux));
  FUNC01_Rom func01_rom_1 (.a(a), .b(b), .c(c), .d(d), .e(e), .x(x_rom));

  // Notes on the sheet:
  //   Boolean function #01: divisibility by N
endmodule

module FUNC01_Gates (
  input  a,
  input  b,
  input  c,
  input  d,
  input  e,
  output x
);

  wire and_1_out, and_2_out, and_3_out, and_4_out, and_5_out, and_6_out, and_7_out, and_8_out, and_9_out,
       and_10_out, and_11_out, not_1_out, not_2_out, not_3_out, not_4_out, not_5_out;

  not not_1 (not_1_out, a);
  not not_2 (not_2_out, b);
  not not_3 (not_3_out, c);
  not not_4 (not_4_out, d);
  not not_5 (not_5_out, e);
  and and_1 (and_1_out, not_1_out, not_2_out, not_3_out, not_4_out, not_5_out);
  and and_2 (and_2_out, not_1_out, not_2_out, not_3_out, d, e);
  and and_3 (and_3_out, not_1_out, not_2_out, c, d, not_5_out);
  and and_4 (and_4_out, not_1_out, b, not_3_out, not_4_out, e);
  and and_5 (and_5_out, not_1_out, b, c, not_4_out, not_5_out);
  and and_6 (and_6_out, not_1_out, b, c, d, e);
  and and_7 (and_7_out, a, not_2_out, not_3_out, d, not_5_out);
  and and_8 (and_8_out, a, not_2_out, c, not_4_out, e);
  and and_9 (and_9_out, a, b, not_3_out, not_4_out, not_5_out);
  and and_10 (and_10_out, a, b, not_3_out, d, e);
  and and_11 (and_11_out, a, b, c, d, not_5_out);
  or or_1 (x, and_1_out, and_2_out, and_3_out, and_4_out, and_5_out, and_6_out, and_7_out, and_8_out, and_9_out, and_10_out, and_11_out);
endmodule

module FUNC01_Mux (
  input  a,
  input  b,
  input  c,
  input  d,
  input  e,
  output x
);

  Pull_Resistor pull_resistor_1 (.node(x));
endmodule

module FUNC01_Demux (
  input  a,
  input  b,
  input  c,
  input  d,
  input  e,
  output x
);

  Pull_Resistor pull_resistor_1 (.node(x));
endmodule

module FUNC01_Rom (
  input  a,
  input  b,
  input  c,
  input  d,
  input  e,
  output x
);

  Pull_Resistor pull_resistor_1 (.node(x));
endmodule
