// Logisim project rs_latch_example.circ as structural Verilog: 1 circuit, main circuit main
module main (
  input  R,
  input  S,
  output Q,
  output nQ,
  output Eq
);

  wire and_1_out;

  nor nor_1 (Q, nQ, R);
  nor nor_2 (nQ, Q, S);
  or or_1 (Eq, S, and_1_out);
  and and_1 (and_1_out, ~R, Q);  // AND_Gate

  // Notes on the sheet:
  //   RS Latch implementation with NOR gates
  //   RS Latch characterisitc equation
endmodule
